// Logisim project Logisim_Pipelined Processor.circ as structural Verilog: 15 circuits, main circuit main
module main (
  input  Reset,
  input  [3:0] Display_Address
);

  wire alu_1_is, alu_1_is_2, Clock, control_unit_1_isbeq, control_unit_1_isbgt, control_unit_1_iscall,
       control_unit_1_isimmediate, control_unit_1_isld, control_unit_1_isret, control_unit_1_isst,
       control_unit_1_isubranch, control_unit_1_iswb, data_lock_unit_1_data_lock_conflict,
       ex_ma_latch_1_out_16, ex_ma_latch_1_out_17, ex_ma_latch_1_out_18, ex_ma_latch_1_out_19,
       flags_1_flags_e, flags_1_flags_gt, isBranchTaken, isWb, of_ex_latch_1_out_27, of_ex_latch_1_out_28,
       of_ex_latch_1_out_29, of_ex_latch_1_out_30, of_ex_latch_1_out_31, of_ex_latch_1_out_32,
       of_ex_latch_1_out_33, of_ex_latch_1_out_34, or_1_out, RW__EX_op2, RW__MA_op2, RW__OF_op1, RW__OF_op2,
       Stall;
  wire [1:0] ma_rw_latch_1_out_15, RW_MA__EX_op1, RW_MA__EX_op2;
  wire [3:0] if_of_latch_1_out_7_2, if_of_latch_1_out_7_3, if_of_latch_1_out_7_4, ma_rw_latch_1_out_14_2,
       multiplexer_12_out, multiplexer_14_out, \reg ;
  wire [4:0] if_of_latch_1_out_7_5;
  wire [12:0] control_unit_1_alusignals, of_ex_latch_1_out_26;
  wire [26:0] if_of_latch_1_out_7;
  wire [31:0] adder_1_out, adder_2_out, adder_3_out, alu_1_aluresult, aluResult, bit_extender_1_out,
       bit_extender_2_out, bit_extender_3_out, branchTarget, data, EX_MA_Instruction, ex_ma_latch_1_out_12,
       ex_ma_latch_1_out_14, ex_ma_latch_1_out_15, IF_OF_Instruction, if_of_latch_1_out_8, MA_RW_Instruction,
       ma_rw_latch_1_out_11, ma_rw_latch_1_out_12, ma_rw_latch_1_out_13, ma_rw_latch_1_out_14,
       memory_unit_1_ldresult, multiplexer_1_out, multiplexer_2_out, multiplexer_3_out, multiplexer_5_out,
       multiplexer_7_out, multiplexer_9_out, multiplexer_10_out, multiplexer_11_out, multiplexer_13_out,
       multiplexer_15_out, OF_EX_Instruction, of_ex_latch_1_out_20, of_ex_latch_1_out_21,
       of_ex_latch_1_out_22, of_ex_latch_1_out_23, of_ex_latch_1_out_24, of_ex_latch_1_out_25, PC_q,
       register_file_1_displayd, register_file_1_readd1, register_file_1_readd2, rom_1_data, shifter_1_out,
       shifter_2_out;

  MA_RW_Latch ma_rw_latch_1 (
    .in_9(Reset), .out_10(MA_RW_Instruction), .in_8(Clock), .in_4(ex_ma_latch_1_out_12),
    .in_5(memory_unit_1_ldresult), .in_6(aluResult), .in_7(ex_ma_latch_1_out_15),
    .isLd(ex_ma_latch_1_out_16), .isCall(ex_ma_latch_1_out_18), .isWb(ex_ma_latch_1_out_19),
    .out_11(ma_rw_latch_1_out_11), .out_12(ma_rw_latch_1_out_12), .out_13(ma_rw_latch_1_out_13),
    .out_14({ma_rw_latch_1_out_14[31:26], ma_rw_latch_1_out_14_2, ma_rw_latch_1_out_14[21:0]}),
    .out_15(ma_rw_latch_1_out_15[0]), .out_16(ma_rw_latch_1_out_15[1]), .out_17(isWb));
  EX_MA_Latch ex_ma_latch_1 (
    .in_10(Reset), .out_11(EX_MA_Instruction), .in_9(Clock), .in_5(of_ex_latch_1_out_20),
    .in_6(alu_1_aluresult), .in_7(multiplexer_5_out), .in_8(of_ex_latch_1_out_25),
    .isLd(of_ex_latch_1_out_31), .isSt(of_ex_latch_1_out_32), .isCall(of_ex_latch_1_out_33),
    .isWb(of_ex_latch_1_out_34), .out_12(ex_ma_latch_1_out_12), .out_13(aluResult),
    .out_14(ex_ma_latch_1_out_14), .out_15(ex_ma_latch_1_out_15), .out_16(ex_ma_latch_1_out_16),
    .out_17(ex_ma_latch_1_out_17), .out_18(ex_ma_latch_1_out_18), .out_19(ex_ma_latch_1_out_19));
  Register #(.width(32)) PC (.D(multiplexer_2_out), .en(Stall), .Q(PC_q), .clk(Clock), .clr(Reset));
  IF_OF_Latch if_of_latch_1 (
    .in_5(Reset), .out_6(IF_OF_Instruction), .in_4(Clock), .in_2(PC_q), .in_3(multiplexer_9_out),
    .Stall(Stall), .out_8(if_of_latch_1_out_8),
    .out_7({if_of_latch_1_out_7_5, if_of_latch_1_out_7[26], if_of_latch_1_out_7_4, if_of_latch_1_out_7_3, if_of_latch_1_out_7_2, if_of_latch_1_out_7[13:0]}));
  assign bit_extender_1_out = {{5{if_of_latch_1_out_7[26]}}, {if_of_latch_1_out_7[26], if_of_latch_1_out_7_4, if_of_latch_1_out_7_3, if_of_latch_1_out_7_2, if_of_latch_1_out_7[13:0]}};  // Bit_Extender bit_extender_1
  OF_EX_Latch of_ex_latch_1 (
    .in_1(control_unit_1_isret), .in_2(control_unit_1_alusignals), .Bubble(or_1_out),
    .in_11(if_of_latch_1_out_8), .in_12(adder_3_out), .in_13(multiplexer_11_out), .in_14(multiplexer_15_out),
    .in_15(multiplexer_13_out),
    .isRet({if_of_latch_1_out_7_5, if_of_latch_1_out_7[26], if_of_latch_1_out_7_4, if_of_latch_1_out_7_3, if_of_latch_1_out_7_2, if_of_latch_1_out_7[13:0]}),
    .in_3(control_unit_1_isbeq), .isBgt(control_unit_1_isbgt), .isUBranch(control_unit_1_isubranch),
    .isLd(control_unit_1_isld), .isSt(control_unit_1_isst), .in_8(control_unit_1_iscall),
    .in_9(control_unit_1_iswb), .out_19(OF_EX_Instruction), .in_17(Clock), .in_18(Reset),
    .out_20(of_ex_latch_1_out_20), .out_21(of_ex_latch_1_out_21), .out_22(of_ex_latch_1_out_22),
    .out_23(of_ex_latch_1_out_23), .out_24(of_ex_latch_1_out_24), .out_25(of_ex_latch_1_out_25),
    .out_26(of_ex_latch_1_out_26), .out_27(of_ex_latch_1_out_27), .out_28(of_ex_latch_1_out_28),
    .out_29(of_ex_latch_1_out_29), .out_30(of_ex_latch_1_out_30), .out_31(of_ex_latch_1_out_31),
    .out_32(of_ex_latch_1_out_32), .out_33(of_ex_latch_1_out_33), .out_34(of_ex_latch_1_out_34));
  Multiplexer #(.select(2), .width(32), .enable("false")) multiplexer_1 (
    .in0(of_ex_latch_1_out_22), .in1(data), .in2(aluResult), .in3(aluResult), .out(multiplexer_1_out),
    .sel(RW_MA__EX_op2));
  Adder #(.width(32)) adder_1 (.a(ma_rw_latch_1_out_11), .b(32'h4), .out(adder_1_out));  // open: cin, cout
  Multiplexer #(.width(32), .enable("false")) multiplexer_2 (
    .in0(adder_2_out), .in1(branchTarget), .out(multiplexer_2_out), .sel(isBranchTaken));
  Adder #(.width(32)) adder_2 (.a(32'h4), .b(PC_q), .out(adder_2_out));  // open: cin, cout
  Shifter #(.width(32)) shifter_1 (.in(bit_extender_1_out), .\dist (5'b00010), .out(shifter_1_out));
  Multiplexer #(.select(2), .width(32), .enable("false")) multiplexer_3 (
    .in0(of_ex_latch_1_out_23), .in1(data), .in2(aluResult), .in3(aluResult), .out(multiplexer_3_out),
    .sel(RW_MA__EX_op1));
  Multiplexer #(.select(2), .width(32), .enable("false")) multiplexer_4 (
    .in0(ma_rw_latch_1_out_13), .in1(ma_rw_latch_1_out_12), .in2(adder_1_out), .out(data),
    .sel(ma_rw_latch_1_out_15));  // open: in3
  Adder #(.width(32)) adder_3 (.a(shifter_1_out), .b(if_of_latch_1_out_8), .out(adder_3_out));  // open: cin, cout
  Multiplexer #(.width(32), .enable("false")) multiplexer_5 (
    .in0(of_ex_latch_1_out_24), .in1(data), .out(multiplexer_5_out), .sel(RW__EX_op2));
  Multiplexer #(.width(32), .enable("false")) multiplexer_6 (
    .in0(of_ex_latch_1_out_21), .in1(multiplexer_3_out), .out(branchTarget), .sel(of_ex_latch_1_out_27));
  ALU alu_1 (
    .A(multiplexer_3_out), .B(multiplexer_1_out), .ALUsignals(of_ex_latch_1_out_26),
    .aluResult(alu_1_aluresult), .is(alu_1_is), .is_2(alu_1_is_2));
  Memory_Unit memory_unit_1 (
    .MAR(aluResult), .MDR(multiplexer_7_out), .ldResult(memory_unit_1_ldresult), .isSt(ex_ma_latch_1_out_17),
    .Clock(Clock), .isLd(ex_ma_latch_1_out_16), .Reset(Reset));
  Clock u_Clock (.out(Clock));
  ROM #(.addrWidth(24), .dataWidth(32)) rom_1 (.addr(PC_q[25:2]), .data(rom_1_data));  // open: sel
  Multiplexer #(.width(32), .enable("false")) multiplexer_7 (
    .in0(ex_ma_latch_1_out_14), .in1(data), .out(multiplexer_7_out), .sel(RW__MA_op2));
  assign bit_extender_2_out = {{16{1'b0}}, {if_of_latch_1_out_7_2[1:0], if_of_latch_1_out_7[13:0]}};  // Bit_Extender bit_extender_2
  Flags flags_1 (
    .isCmp(of_ex_latch_1_out_26[0]), .is(alu_1_is), .is_2(alu_1_is_2), .flags_GT(flags_1_flags_gt),
    .flags_E(flags_1_flags_e));
  Multiplexer #(.width(4), .enable("false")) multiplexer_8 (
    .in0(ma_rw_latch_1_out_14_2), .in1(4'b1111), .out(\reg ), .sel(ma_rw_latch_1_out_15[1]));
  assign bit_extender_3_out = {{16{if_of_latch_1_out_7_2[1]}}, {if_of_latch_1_out_7_2[1:0], if_of_latch_1_out_7[13:0]}};  // Bit_Extender bit_extender_3
  Multiplexer #(.width(32), .enable("false")) multiplexer_9 (
    .in0(rom_1_data), .in1(32'h68000000), .out(multiplexer_9_out), .sel(isBranchTaken));
  Shifter #(.width(32)) shifter_2 (.in(bit_extender_2_out), .\dist (5'b10000), .out(shifter_2_out));
  or or_1 (or_1_out, isBranchTaken, ~Stall);  // OR_Gate
  Branch_Unit branch_unit_1 (
    .isUBranch(of_ex_latch_1_out_30), .isBeq(of_ex_latch_1_out_28), .flags_E(flags_1_flags_e),
    .isBgt(of_ex_latch_1_out_29), .flags_GT(flags_1_flags_gt), .isBranchTaken(isBranchTaken));
  Multiplexer #(.select(2), .width(32), .enable("false")) multiplexer_10 (
    .in0(bit_extender_3_out), .in1(bit_extender_2_out), .in2(shifter_2_out), .out(multiplexer_10_out),
    .sel(if_of_latch_1_out_7_2[3:2]));  // open: in3
  Multiplexer #(.width(32), .enable("false")) multiplexer_11 (
    .in0(multiplexer_13_out), .in1(multiplexer_10_out), .out(multiplexer_11_out),
    .sel(control_unit_1_isimmediate));
  Multiplexer #(.width(4), .enable("false")) multiplexer_12 (
    .in0(if_of_latch_1_out_7_2), .in1(if_of_latch_1_out_7_4), .out(multiplexer_12_out),
    .sel(control_unit_1_isst));
  Multiplexer #(.width(32), .enable("false")) multiplexer_13 (
    .in0(register_file_1_readd2), .in1(data), .out(multiplexer_13_out), .sel(RW__OF_op2));
  Multiplexer #(.width(4), .enable("false")) multiplexer_14 (
    .in0(if_of_latch_1_out_7_3), .in1(4'b1111), .out(multiplexer_14_out), .sel(control_unit_1_isret));
  Multiplexer #(.width(32), .enable("false")) multiplexer_15 (
    .in0(register_file_1_readd1), .in1(data), .out(multiplexer_15_out), .sel(RW__OF_op1));
  Data_Lock_Unit data_lock_unit_1 (
    .IF_OF(IF_OF_Instruction), .OF_EX(OF_EX_Instruction),
    .Data_Lock_Conflict(data_lock_unit_1_data_lock_conflict));
  Hex_Digit_Display hex_digit_display_1 (.value(register_file_1_displayd[31:28]));  // open: dp
  Control_Unit control_unit_1 (
    .I_bit(if_of_latch_1_out_7[26]), .opcode(if_of_latch_1_out_7_5), .isSt(control_unit_1_isst),
    .isLd(control_unit_1_isld), .isBeq(control_unit_1_isbeq), .isBgt(control_unit_1_isbgt),
    .isRet(control_unit_1_isret), .isImmediate(control_unit_1_isimmediate), .isWb(control_unit_1_iswb),
    .isUbranch(control_unit_1_isubranch), .isCall(control_unit_1_iscall),
    .ALUsignals(control_unit_1_alusignals));
  not not_1 (Stall, data_lock_unit_1_data_lock_conflict);
  Forwarding_Unit forwarding_unit_1 (
    .MA_RW(MA_RW_Instruction), .EX_MA(EX_MA_Instruction), .OF_EX(OF_EX_Instruction),
    .IF_OF(IF_OF_Instruction), .RW__MA_op2(RW__MA_op2), .RW_MA__EX_op2(RW_MA__EX_op2),
    .RW__EX_op2(RW__EX_op2), .RW_MA__EX_op1(RW_MA__EX_op1), .RW__OF_op2(RW__OF_op2), .RW__OF_op1(RW__OF_op1));
  Hex_Digit_Display hex_digit_display_2 (.value(register_file_1_displayd[27:24]));  // open: dp
  Register_File register_file_1 (
    .WriteD(data), .WriteE(isWb), .ReadD1(register_file_1_readd1), .ReadD2(register_file_1_readd2),
    .DisplayD(register_file_1_displayd), .Clock(Clock), .Reset(Reset), .WriteA(\reg ),
    .ReadA1(multiplexer_14_out), .ReadA2(multiplexer_12_out), .DisplayA(Display_Address));
  Hex_Digit_Display hex_digit_display_3 (.value(register_file_1_displayd[23:20]));  // open: dp
  Hex_Digit_Display hex_digit_display_4 (.value(register_file_1_displayd[19:16]));  // open: dp
  Hex_Digit_Display hex_digit_display_5 (.value(register_file_1_displayd[15:12]));  // open: dp
  Hex_Digit_Display hex_digit_display_6 (.value(register_file_1_displayd[11:8]));  // open: dp
  Hex_Digit_Display hex_digit_display_7 (.value(register_file_1_displayd[7:4]));  // open: dp
  Hex_Digit_Display hex_digit_display_8 (.value(register_file_1_displayd[3:0]));  // open: dp

  // Notes on the sheet:
  //   pc+4
  //   branchTarget
  //   pc
  //   data
  //   offset
  //   MDR
  //   MAR
  //   ldResult
  //   isLd
  //   isCall
  //   Instruction Memory
  //   isRet
  //   isLd
  //   isSt
  //   contents of rom_1 (hex, n*v repeats v):
  //   4c400009 4c800006 4cc00000 7c4c0004 758c0004 7c8c0008 760c0008 e18000 90000000
  //   modifier bits
  //   default
  //   unsigned
  //   high
  //   rd
  //   isSt
  //   op2
  //   isImmediate
  //   op1
  //   Display Register
endmodule

module IF_OF_Latch (
  input  Stall,
  input  [31:0] in_2,
  input  [31:0] in_3,
  input  in_4,
  input  in_5,
  output [31:0] out_6,
  output [31:0] out_7,
  output [31:0] out_8
);

  Register #(.width(32)) register_1 (.D(in_2), .en(Stall), .Q(out_8), .clk(in_4), .clr(in_5));
  Register #(.width(32)) register_2 (.D(in_3), .en(Stall), .Q(out_6), .clk(in_4), .clr(in_5));

  assign out_7 = out_6;
endmodule

module Control_Unit (
  input  I_bit,
  input  [4:0] opcode,
  output isSt,
  output isLd,
  output isBeq,
  output isBgt,
  output isRet,
  output isImmediate,
  output isWb,
  output isUbranch,
  output isCall,
  output [12:0] ALUsignals
);

  wire and_6_out, and_7_out, and_8_out, and_9_out, and_10_out, and_12_out, and_13_out, nand_1_out;

  nand nand_1 (nand_1_out, opcode[0], opcode[1]);
  and and_1 (isSt, opcode[0], opcode[1], opcode[2], opcode[3], ~opcode[4]);  // AND_Gate
  and and_2 (isLd, ~opcode[0], opcode[1], opcode[2], opcode[3], ~opcode[4]);  // AND_Gate
  and and_3 (isBeq, ~opcode[0], ~opcode[1], ~opcode[2], ~opcode[3], opcode[4]);  // AND_Gate
  and and_4 (isBgt, opcode[0], ~opcode[1], ~opcode[2], ~opcode[3], opcode[4]);  // AND_Gate
  and and_5 (isRet, ~opcode[0], ~opcode[1], opcode[2], ~opcode[3], opcode[4]);  // AND_Gate
  and and_6 (and_6_out, opcode[0], ~opcode[1], opcode[2], ~opcode[4]);  // AND_Gate
  and and_7 (and_7_out, opcode[0], opcode[2], opcode[3], ~opcode[4]);  // AND_Gate
  and and_8 (and_8_out, opcode[4], nand_1_out);
  and and_9 (and_9_out, opcode[1], ~opcode[2], ~opcode[3], opcode[4]);  // AND_Gate
  and and_10 (and_10_out, ~opcode[0], ~opcode[1], opcode[2], ~opcode[3], opcode[4]);  // AND_Gate
  and and_11 (isCall, opcode[0], opcode[1], ~opcode[2], ~opcode[3], opcode[4]);  // AND_Gate
  and and_12 (and_12_out, ~opcode[0], ~opcode[1], ~opcode[2], ~opcode[3], ~opcode[4]);  // AND_Gate
  and and_13 (and_13_out, opcode[1], opcode[2], opcode[3], ~opcode[4]);  // AND_Gate
  and isSub (ALUsignals[2], opcode[0], ~opcode[1], ~opcode[2], ~opcode[3], ~opcode[4]);  // AND_Gate
  and isCmp (ALUsignals[0], opcode[0], ~opcode[1], opcode[2], ~opcode[3], ~opcode[4]);  // AND_Gate
  and isMul (ALUsignals[3], ~opcode[0], opcode[1], ~opcode[2], ~opcode[3], ~opcode[4]);  // AND_Gate
  and isDiv (ALUsignals[4], opcode[0], opcode[1], ~opcode[2], ~opcode[3], ~opcode[4]);  // AND_Gate
  and isMod (ALUsignals[5], ~opcode[0], ~opcode[1], opcode[2], ~opcode[3], ~opcode[4]);  // AND_Gate
  and isLsl (ALUsignals[7], ~opcode[0], opcode[1], ~opcode[2], opcode[3], ~opcode[4]);  // AND_Gate
  and isLsr (ALUsignals[8], opcode[0], opcode[1], ~opcode[2], opcode[3], ~opcode[4]);  // AND_Gate
  and isAsr (ALUsignals[9], ~opcode[0], ~opcode[1], opcode[2], opcode[3], ~opcode[4]);  // AND_Gate
  and isOr (ALUsignals[12], opcode[0], opcode[1], opcode[2], ~opcode[3], ~opcode[4]);  // AND_Gate
  and isAnd (ALUsignals[11], ~opcode[0], opcode[1], opcode[2], ~opcode[3], ~opcode[4]);  // AND_Gate
  and isNot (ALUsignals[10], ~opcode[0], ~opcode[1], ~opcode[2], opcode[3], ~opcode[4]);  // AND_Gate
  and isMov (ALUsignals[6], opcode[0], ~opcode[1], ~opcode[2], opcode[3], ~opcode[4]);  // AND_Gate
  or or_1 (isUbranch, and_9_out, and_10_out);
  or isAdd (ALUsignals[1], and_12_out, and_13_out);
  nor nor_1 (isWb, and_6_out, and_7_out, and_8_out);

  assign isImmediate = I_bit;

  // Notes on the sheet:
  //   op1
  //   op2
  //   op3
  //   op4
  //   op5
endmodule

module Register_File (
  input  Clock,
  input  Reset,
  input  [31:0] WriteD,
  input  [3:0] ReadA1,
  input  WriteE,
  input  [3:0] WriteA,
  input  [3:0] ReadA2,
  input  [3:0] DisplayA,
  output [31:0] ReadD1,
  output [31:0] ReadD2,
  output [31:0] DisplayD
);

  wire demultiplexer_1_out0, demultiplexer_1_out1, demultiplexer_1_out2, demultiplexer_1_out3,
       demultiplexer_1_out4, demultiplexer_1_out5, demultiplexer_1_out6, demultiplexer_1_out7,
       demultiplexer_1_out8, demultiplexer_1_out9, demultiplexer_1_out10, demultiplexer_1_out11,
       demultiplexer_1_out12, demultiplexer_1_out13, demultiplexer_1_out14, demultiplexer_1_out15,
       multiplexer_2_out, or_1_out, or_2_out;
  wire [31:0] multiplexer_1_out, r0_q, r1_q, r2_q, r3_q, r4_q, r5_q, r6_q, r7_q, r8_q, r9_q, r10_q, r11_q,
       r12_q, r13_q, r14_q, r15_q;

  Demultiplexer #(.select(4), .disabled(0), .enable("false")) demultiplexer_1 (
    .out0(demultiplexer_1_out0), .out1(demultiplexer_1_out1), .out2(demultiplexer_1_out2),
    .out3(demultiplexer_1_out3), .out4(demultiplexer_1_out4), .out5(demultiplexer_1_out5),
    .out6(demultiplexer_1_out6), .out7(demultiplexer_1_out7), .out8(demultiplexer_1_out8),
    .out9(demultiplexer_1_out9), .out10(demultiplexer_1_out10), .out11(demultiplexer_1_out11),
    .out12(demultiplexer_1_out12), .out13(demultiplexer_1_out13), .out14(demultiplexer_1_out14),
    .out15(demultiplexer_1_out15), .in(WriteE), .sel(WriteA));
  Multiplexer #(.width(32), .enable("false")) multiplexer_1 (
    .in0(WriteD), .in1(32'h3fffffc), .out(multiplexer_1_out), .sel(Reset));
  or or_1 (or_1_out, demultiplexer_1_out14, Reset);
  Multiplexer #(.enable("false")) multiplexer_2 (.in0(or_2_out), .out(multiplexer_2_out), .sel(1'b0));  // open: in1
  or or_2 (or_2_out, Clock, Reset);
  Register #(.width(32)) r0 (.D(WriteD), .en(demultiplexer_1_out0), .Q(r0_q), .clk(Clock), .clr(Reset));
  Register #(.width(32)) r1 (.D(WriteD), .en(demultiplexer_1_out1), .Q(r1_q), .clk(Clock), .clr(Reset));
  Register #(.width(32)) r2 (.D(WriteD), .en(demultiplexer_1_out2), .Q(r2_q), .clk(Clock), .clr(Reset));
  Register #(.width(32)) r3 (.D(WriteD), .en(demultiplexer_1_out3), .Q(r3_q), .clk(Clock), .clr(Reset));
  Register #(.width(32)) r4 (.D(WriteD), .en(demultiplexer_1_out4), .Q(r4_q), .clk(Clock), .clr(Reset));
  Register #(.width(32)) r5 (.D(WriteD), .en(demultiplexer_1_out5), .Q(r5_q), .clk(Clock), .clr(Reset));
  Register #(.width(32)) r6 (.D(WriteD), .en(demultiplexer_1_out6), .Q(r6_q), .clk(Clock), .clr(Reset));
  Register #(.width(32)) r7 (.D(WriteD), .en(demultiplexer_1_out7), .Q(r7_q), .clk(Clock), .clr(Reset));
  Register #(.width(32)) r8 (.D(WriteD), .en(demultiplexer_1_out8), .Q(r8_q), .clk(Clock), .clr(Reset));
  Register #(.width(32)) r9 (.D(WriteD), .en(demultiplexer_1_out9), .Q(r9_q), .clk(Clock), .clr(Reset));
  Register #(.width(32)) r10 (.D(WriteD), .en(demultiplexer_1_out10), .Q(r10_q), .clk(Clock), .clr(Reset));
  Register #(.width(32)) r11 (.D(WriteD), .en(demultiplexer_1_out11), .Q(r11_q), .clk(Clock), .clr(Reset));
  Register #(.width(32)) r12 (.D(WriteD), .en(demultiplexer_1_out12), .Q(r12_q), .clk(Clock), .clr(Reset));
  Register #(.width(32)) r13 (.D(WriteD), .en(demultiplexer_1_out13), .Q(r13_q), .clk(Clock), .clr(Reset));
  Register #(.width(32)) r14 (.D(multiplexer_1_out), .en(or_1_out), .Q(r14_q), .clk(multiplexer_2_out));  // open: clr
  Register #(.width(32)) r15 (.D(WriteD), .en(demultiplexer_1_out15), .Q(r15_q), .clk(Clock), .clr(Reset));
  Multiplexer #(.select(4), .width(32), .disabled(0), .enable("false")) multiplexer_3 (
    .in0(r0_q), .in1(r1_q), .in2(r2_q), .in3(r3_q), .in4(r4_q), .in5(r5_q), .in6(r6_q), .in7(r7_q),
    .in8(r8_q), .in9(r9_q), .in10(r10_q), .in11(r11_q), .in12(r12_q), .in13(r13_q), .in14(r14_q),
    .in15(r15_q), .out(ReadD1), .sel(ReadA1));
  Multiplexer #(.select(4), .width(32), .disabled(0), .enable("false")) multiplexer_4 (
    .in0(r0_q), .in1(r1_q), .in2(r2_q), .in3(r3_q), .in4(r4_q), .in5(r5_q), .in6(r6_q), .in7(r7_q),
    .in8(r8_q), .in9(r9_q), .in10(r10_q), .in11(r11_q), .in12(r12_q), .in13(r13_q), .in14(r14_q),
    .in15(r15_q), .out(ReadD2), .sel(ReadA2));
  Multiplexer #(.select(4), .width(32), .disabled(0), .enable("false")) multiplexer_5 (
    .in0(r0_q), .in1(r1_q), .in2(r2_q), .in3(r3_q), .in4(r4_q), .in5(r5_q), .in6(r6_q), .in7(r7_q),
    .in8(r8_q), .in9(r9_q), .in10(r10_q), .in11(r11_q), .in12(r12_q), .in13(r13_q), .in14(r14_q),
    .in15(r15_q), .out(DisplayD), .sel(DisplayA));
endmodule

module OF_EX_Latch (
  input  in_1,
  input  [12:0] in_2,
  input  in_3,
  input  isBgt,
  input  isUBranch,
  input  isLd,
  input  isSt,
  input  in_8,
  input  in_9,
  input  Bubble,
  input  [31:0] in_11,
  input  [31:0] in_12,
  input  [31:0] in_13,
  input  [31:0] in_14,
  input  [31:0] in_15,
  input  [31:0] isRet,
  input  in_17,
  input  in_18,
  output [31:0] out_19,
  output [31:0] out_20,
  output [31:0] out_21,
  output [31:0] out_22,
  output [31:0] out_23,
  output [31:0] out_24,
  output [31:0] out_25,
  output [12:0] out_26,
  output out_27,
  output out_28,
  output out_29,
  output out_30,
  output out_31,
  output out_32,
  output out_33,
  output out_34
);

  wire [31:0] multiplexer_1_out;

  Register #(.width(32)) register_1 (.D(in_11), .Q(out_20), .clk(in_17), .clr(in_18));  // open: en
  Register #(.width(32)) register_2 (.D(in_12), .Q(out_21), .clk(in_17), .clr(in_18));  // open: en
  Register #(.width(32)) register_3 (.D(in_13), .Q(out_22), .clk(in_17), .clr(in_18));  // open: en
  Register #(.width(32)) register_4 (.D(in_14), .Q(out_23), .clk(in_17), .clr(in_18));  // open: en
  Register #(.width(32)) register_5 (.D(in_15), .Q(out_24), .clk(in_17), .clr(in_18));  // open: en
  Multiplexer #(.width(32), .enable("false")) multiplexer_1 (
    .in0(isRet), .in1(32'h68000000), .out(multiplexer_1_out), .sel(Bubble));
  Register #(.width(32)) register_6 (.D(multiplexer_1_out), .Q(out_19), .clk(in_17), .clr(in_18));  // open: en
  Control control_1 (
    .Bubble(Bubble), .in_11(in_17), .in_12(in_18), .isRet(in_1), .in_9(in_2), .in_1(in_3), .isBgt(isBgt),
    .isUBranch(isUBranch), .isLd(isLd), .isSt(isSt), .in_6(in_8), .in_7(in_9), .out_14(out_27),
    .out_13(out_26), .out_15(out_28), .out_16(out_29), .out_17(out_30), .out_18(out_31), .out_19(out_32),
    .out_20(out_33), .out_21(out_34));

  assign out_25 = out_19;

  // Notes on the sheet:
  //   PC
  //   Branch Target
  //   B
  //   A
  //   OP2
  //   INSTRUCTION
  //   ALU Signals
  //   isBeq
  //   isCall
  //   isWb
endmodule

module Branch_Unit (
  input  isUBranch,
  input  isBeq,
  input  flags_E,
  input  isBgt,
  input  flags_GT,
  output isBranchTaken
);

  wire and_1_out, and_2_out;

  and and_1 (and_1_out, isBeq, flags_E);
  and and_2 (and_2_out, isBgt, flags_GT);
  or or_1 (isBranchTaken, isUBranch, and_1_out, and_2_out);
endmodule

module Flags (
  input  isCmp,
  input  is,
  input  is_2,
  output flags_GT,
  output flags_E
);

  D_Flip_Flop #(.trigger("high")) d_ff_1 (.clk(isCmp), .D(is), .Q(flags_GT));  // open: Qn, preset, en, reset
  D_Flip_Flop #(.trigger("high")) d_ff_2 (.clk(isCmp), .D(is_2), .Q(flags_E));  // open: Qn, preset, en, reset
endmodule

module ALU (
  input  [31:0] A,
  input  [31:0] B,
  input  [12:0] ALUsignals,
  output [31:0] aluResult,
  output is,
  output is_2
);

  wire [31:0] adder_1_out, and_1_out, divider_1_out, divider_1_rem, multiplier_1_out, not_1_out, or_1_out,
       shifter_1_out, shifter_2_out, shifter_3_out, subtractor_1_out;

  Adder #(.width(32)) adder_1 (.a(A), .b(B), .out(adder_1_out));  // open: cin, cout
  Subtractor #(.width(32)) subtractor_1 (.a(A), .b(B), .out(subtractor_1_out));  // open: bin, bout
  Multiplier #(.width(32)) multiplier_1 (.a(A), .b(B), .out(multiplier_1_out));  // open: cin, cout
  Divider #(.width(32)) divider_1 (.a(A), .b(B), .out(divider_1_out), .rem(divider_1_rem));  // open: upper
  Comparator #(.width(32)) comparator_1 (.a(A), .b(B), .gt(is), .eq(is_2));  // open: lt
  Shifter #(.width(32)) shifter_1 (.in(A), .\dist (B[4:0]), .out(shifter_1_out));
  Shifter #(.width(32), .shift("lr")) shifter_2 (.in(A), .\dist (B[4:0]), .out(shifter_2_out));
  Shifter #(.width(32), .shift("ar")) shifter_3 (.in(A), .\dist (B[4:0]), .out(shifter_3_out));
  assign not_1_out = ~B;  // NOT_Gate not_1, 32 bits wide
  assign and_1_out = A & B;  // AND_Gate and_1, 32 bits wide
  assign or_1_out = A | B;  // OR_Gate or_1, 32 bits wide
  assign aluResult = ALUsignals[1] ? adder_1_out : 32'bz;  // Controlled_Buffer controlled_buffer_1
  assign aluResult = ALUsignals[2] ? subtractor_1_out : 32'bz;  // Controlled_Buffer controlled_buffer_2
  assign aluResult = ALUsignals[3] ? multiplier_1_out : 32'bz;  // Controlled_Buffer controlled_buffer_3
  assign aluResult = ALUsignals[4] ? divider_1_out : 32'bz;  // Controlled_Buffer controlled_buffer_4
  assign aluResult = ALUsignals[5] ? divider_1_rem : 32'bz;  // Controlled_Buffer controlled_buffer_5
  assign aluResult = ALUsignals[6] ? B : 32'bz;  // Controlled_Buffer controlled_buffer_6
  assign aluResult = ALUsignals[7] ? shifter_1_out : 32'bz;  // Controlled_Buffer controlled_buffer_7
  assign aluResult = ALUsignals[8] ? shifter_2_out : 32'bz;  // Controlled_Buffer controlled_buffer_8
  assign aluResult = ALUsignals[9] ? shifter_3_out : 32'bz;  // Controlled_Buffer controlled_buffer_9
  assign aluResult = ALUsignals[10] ? not_1_out : 32'bz;  // Controlled_Buffer controlled_buffer_10
  assign aluResult = ALUsignals[11] ? and_1_out : 32'bz;  // Controlled_Buffer controlled_buffer_11
  assign aluResult = ALUsignals[12] ? or_1_out : 32'bz;  // Controlled_Buffer controlled_buffer_12

  // Notes on the sheet:
  //   add
  //   sub
  //   mul
  //   div
  //   cmp
  //   lsr
  //   mod
  //   lsl
  //   asr
endmodule

module Data_Lock_Unit (
  input  [31:0] IF_OF,
  input  [31:0] OF_EX,
  output Data_Lock_Conflict
);

  wire and_1_out, and_2_out, isBeq_isB__isBgt__is_isCall_2_out, isBeq_isB__isBgt__is_isCall_out, isLd_out,
       isNop_2_out, isNop_out, isNot__isMov_out, isSt_out, nor_1_out, nor_2_out, nor_3_out, nor_4_out,
       not_1_out, or_1_out;
  wire [3:0] subtractor_1_out, subtractor_2_out;

  Subtractor #(.width(4)) subtractor_1 (.a(OF_EX[25:22]), .b(IF_OF[21:18]), .out(subtractor_1_out));  // open: bin, bout
  Subtractor #(.width(4)) subtractor_2 (.a(OF_EX[25:22]), .b(IF_OF[17:14]), .out(subtractor_2_out));  // open: bin, bout
  nor nor_1 (nor_1_out, subtractor_1_out[3], subtractor_1_out[2], subtractor_1_out[1], subtractor_1_out[0]);
  nor nor_2 (nor_2_out, subtractor_2_out[3], subtractor_2_out[2], subtractor_2_out[1], subtractor_2_out[0]);
  and isBeq_isB__isBgt__is_isCall (isBeq_isB__isBgt__is_isCall_out, IF_OF[31], ~IF_OF[30], ~IF_OF[29]);  // AND_Gate
  and isLd (isLd_out, ~OF_EX[27], OF_EX[28], OF_EX[29], OF_EX[30], ~OF_EX[31]);  // AND_Gate
  and isSt (isSt_out, IF_OF[27], IF_OF[28], IF_OF[29], IF_OF[30], ~IF_OF[31]);  // AND_Gate
  not not_1 (not_1_out, isSt_out);
  and isNop (isNop_out, ~IF_OF[31], IF_OF[30], IF_OF[29], ~IF_OF[28], IF_OF[27]);  // AND_Gate
  nor nor_3 (nor_3_out, isBeq_isB__isBgt__is_isCall_out, isNop_out, isNot__isMov_out);
  and and_1 (and_1_out, nor_1_out, nor_3_out);
  and isNot__isMov (isNot__isMov_out, ~IF_OF[31], IF_OF[30], ~IF_OF[28], ~IF_OF[28]);  // AND_Gate
  and and_2 (and_2_out, nor_2_out, nor_4_out);
  or or_1 (or_1_out, and_2_out, and_1_out);
  and and_3 (Data_Lock_Conflict, or_1_out, isLd_out);
  and isBeq_isB__isBgt__is_isCall_2 (isBeq_isB__isBgt__is_isCall_2_out, IF_OF[31], ~IF_OF[30], ~IF_OF[29]);  // AND_Gate
  and isNop_2 (isNop_2_out, ~IF_OF[31], IF_OF[30], IF_OF[29], ~IF_OF[28], IF_OF[27]);  // AND_Gate
  nor nor_4 (nor_4_out, isBeq_isB__isBgt__is_isCall_2_out, isNop_2_out);
endmodule

module Detect_Conflict (
  input  [31:0] B,
  input  [31:0] A,
  output FO_Conflict,
  output SO_Conflict
);

  wire and_1_out, and_2_out, and_3_out, and_4_out, and_5_out, and_6_out, and_7_out, and_8_out,
       isBeq_isB__isBgt__is_isCall_2_out, isBeq_isB__isBgt__is_isCall_out, isCall_out, isNop_2_out,
       isNop_out, isNot__isMov_out, isRet_out, isSt_out, multiplexer_4_out, nor_1_out, nor_2_out, nor_3_out,
       nor_4_out, nor_5_out, not_1_out;
  wire [3:0] multiplexer_3_out, multiplexer_5_out, multiplexer_6_out, subtractor_1_out, subtractor_2_out;

  and isBeq_isB__isBgt__is_isCall (isBeq_isB__isBgt__is_isCall_out, A[31], ~A[30], ~A[29]);  // AND_Gate
  and isNop (isNop_out, ~A[31], A[30], A[29], ~A[28], A[27]);  // AND_Gate
  nor nor_1 (nor_1_out, isBeq_isB__isBgt__is_isCall_out, isNop_out, isNot__isMov_out);
  and and_1 (and_1_out, nor_1_out, nor_4_out);
  and isNot__isMov (isNot__isMov_out, ~A[31], A[30], ~A[28], ~A[28]);  // AND_Gate
  and isBeq_isB__isBgt__is_isCall_2 (isBeq_isB__isBgt__is_isCall_2_out, A[31], ~A[30], ~A[29]);  // AND_Gate
  nor nor_2 (nor_2_out, isBeq_isB__isBgt__is_isCall_2_out, isNop_2_out);
  and and_2 (and_2_out, nor_2_out, nor_4_out);
  and isNop_2 (isNop_2_out, ~A[31], A[30], A[29], ~A[28], A[27]);  // AND_Gate
  Multiplexer #(.enable("false")) multiplexer_1 (.in0(1'b0), .in1(nor_3_out), .out(FO_Conflict), .sel(and_1_out));
  and and_3 (and_3_out, multiplexer_4_out, nor_5_out);
  Multiplexer #(.enable("false")) multiplexer_2 (.in0(1'b0), .in1(and_3_out), .out(SO_Conflict), .sel(and_2_out));
  and isRet (isRet_out, A[31], ~A[30], A[29], ~A[28], ~A[27]);  // AND_Gate
  Multiplexer #(.width(4), .enable("false")) multiplexer_3 (
    .in0(A[21:18]), .in1(4'b1111), .out(multiplexer_3_out), .sel(isRet_out));
  and isSt (isSt_out, ~A[31], A[30], A[29], A[28], A[27]);  // AND_Gate
  not not_1 (not_1_out, A[26]);
  Multiplexer #(.enable("false")) multiplexer_4 (.in0(not_1_out), .in1(1'b1), .out(multiplexer_4_out), .sel(isSt_out));
  Subtractor #(.width(4)) subtractor_1 (
    .a(multiplexer_6_out), .b(multiplexer_3_out), .out(subtractor_1_out));  // open: bin, bout
  Multiplexer #(.width(4), .enable("false")) multiplexer_5 (
    .in0(A[17:14]), .in1(A[25:22]), .out(multiplexer_5_out), .sel(isSt_out));
  nor nor_3 (nor_3_out, subtractor_1_out[3], subtractor_1_out[2], subtractor_1_out[1], subtractor_1_out[0]);
  and and_4 (and_4_out, ~B[31], B[29], ~B[28], B[27]);  // AND_Gate
  Subtractor #(.width(4)) subtractor_2 (
    .a(multiplexer_5_out), .b(multiplexer_6_out), .out(subtractor_2_out));  // open: bin, bout
  and and_5 (and_5_out, ~B[31], B[30], B[29], B[27]);  // AND_Gate
  nor nor_4 (nor_4_out, and_4_out, and_5_out, and_6_out, and_7_out, and_8_out);
  nor nor_5 (nor_5_out, subtractor_2_out[3], subtractor_2_out[2], subtractor_2_out[1], subtractor_2_out[0]);
  and and_6 (and_6_out, B[31], ~B[30], ~B[29], ~B[28]);  // AND_Gate
  and and_7 (and_7_out, B[31], ~B[30], ~B[29], ~B[27]);  // AND_Gate
  and and_8 (and_8_out, B[31], ~B[30], ~B[28], ~B[27]);  // AND_Gate
  and isCall (isCall_out, B[31], ~B[30], ~B[29], B[28], B[27]);  // AND_Gate
  Multiplexer #(.width(4), .enable("false")) multiplexer_6 (
    .in0(B[25:22]), .in1(4'b1111), .out(multiplexer_6_out), .sel(isCall_out));

  // Notes on the sheet:
  //   hassrc2
  //   A.rs1
  //   ra
  //   A.I
  //   A.rs2
  //   A.rd
  //   ra
  //   rd
endmodule

module Forwarding_Unit (
  input  [31:0] MA_RW,
  input  [31:0] EX_MA,
  input  [31:0] OF_EX,
  input  [31:0] IF_OF,
  output RW__OF_op2,
  output RW__OF_op1,
  output [1:0] RW_MA__EX_op1,
  output RW__EX_op2,
  output RW__MA_op2,
  output [1:0] RW_MA__EX_op2
);

  wire and_1_out, detect_conflict_2_so_conflict;

  Detect_Conflict detect_conflict_1 (.A(EX_MA), .B(MA_RW), .SO_Conflict(RW__MA_op2));  // open: FO_Conflict
  Detect_Conflict detect_conflict_2 (
    .A(OF_EX), .B(EX_MA), .FO_Conflict(RW_MA__EX_op1[1]), .SO_Conflict(detect_conflict_2_so_conflict));
  and and_1 (and_1_out, ~OF_EX[31], OF_EX[30], OF_EX[29], OF_EX[28], OF_EX[27]);  // AND_Gate
  Multiplexer #(.enable("false")) multiplexer_1 (
    .in0(detect_conflict_2_so_conflict), .in1(1'b0), .out(RW_MA__EX_op2[1]), .sel(and_1_out));
  Detect_Conflict detect_conflict_3 (.A(OF_EX), .B(MA_RW), .FO_Conflict(RW_MA__EX_op1[0]), .SO_Conflict(RW__EX_op2));
  Multiplexer #(.enable("false")) multiplexer_2 (.in0(RW__EX_op2), .in1(1'b0), .out(RW_MA__EX_op2[0]), .sel(and_1_out));
  Detect_Conflict detect_conflict_4 (.A(IF_OF), .B(MA_RW), .FO_Conflict(RW__OF_op1), .SO_Conflict(RW__OF_op2));

  // Notes on the sheet:
  //   RW->MA
  //   MA->EX
  //   RW->EX
  //   RW->OF
endmodule

module Memory_Unit (
  input  [31:0] MAR,
  input  isLd,
  input  [31:0] MDR,
  input  isSt,
  input  Clock,
  input  Reset,
  output [31:0] ldResult
);

  RAM #(.addrWidth(24), .dataWidth(32), .bus("separate")) ram_1 (
    .addr(MAR[25:2]), .din(MDR), .data(ldResult), .str(isSt), .clk(Clock), .ld(isLd), .clr(Reset));  // open: sel
endmodule

module EX_MA_Latch (
  input  isCall,
  input  isLd,
  input  isSt,
  input  isWb,
  input  [31:0] in_5,
  input  [31:0] in_6,
  input  [31:0] in_7,
  input  [31:0] in_8,
  input  in_9,
  input  in_10,
  output [31:0] out_11,
  output [31:0] out_12,
  output [31:0] out_13,
  output [31:0] out_14,
  output [31:0] out_15,
  output out_16,
  output out_17,
  output out_18,
  output out_19
);

  Register #(.width(32)) register_1 (.D(in_5), .Q(out_12), .clk(in_9), .clr(in_10));  // open: en
  Register #(.width(32)) register_2 (.D(in_6), .Q(out_13), .clk(in_9), .clr(in_10));  // open: en
  Register #(.width(32)) register_3 (.D(in_7), .Q(out_14), .clk(in_9), .clr(in_10));  // open: en
  Register #(.width(32)) register_4 (.D(in_8), .Q(out_11), .clk(in_9), .clr(in_10));  // open: en
  Register #(.width(1)) register_5 (.D(isLd), .Q(out_16), .clk(in_9), .clr(in_10));  // open: en
  Register #(.width(1)) register_6 (.D(isSt), .Q(out_17), .clk(in_9), .clr(in_10));  // open: en
  Register #(.width(1)) register_7 (.D(isCall), .Q(out_18), .clk(in_9), .clr(in_10));  // open: en
  Register #(.width(1)) register_8 (.D(isWb), .Q(out_19), .clk(in_9), .clr(in_10));  // open: en

  assign out_15 = out_11;

  // Notes on the sheet:
  //   PC
  //   Alu Result
  //   OP2
  //   INSTRUCTION
endmodule

module MA_RW_Latch (
  input  isCall,
  input  isLd,
  input  isWb,
  input  [31:0] in_4,
  input  [31:0] in_5,
  input  [31:0] in_6,
  input  [31:0] in_7,
  input  in_8,
  input  in_9,
  output [31:0] out_10,
  output [31:0] out_11,
  output [31:0] out_12,
  output [31:0] out_13,
  output [31:0] out_14,
  output out_15,
  output out_16,
  output out_17
);

  Register #(.width(32)) register_1 (.D(in_4), .Q(out_11), .clk(in_8), .clr(in_9));  // open: en
  Register #(.width(32)) register_2 (.D(in_5), .Q(out_12), .clk(in_8), .clr(in_9));  // open: en
  Register #(.width(32)) register_3 (.D(in_6), .Q(out_13), .clk(in_8), .clr(in_9));  // open: en
  Register #(.width(32)) register_4 (.D(in_7), .Q(out_10), .clk(in_8), .clr(in_9));  // open: en
  Register #(.width(1)) register_5 (.D(isLd), .Q(out_15), .clk(in_8), .clr(in_9));  // open: en
  Register #(.width(1)) register_6 (.D(isCall), .Q(out_16), .clk(in_8), .clr(in_9));  // open: en
  Register #(.width(1)) register_7 (.D(isWb), .Q(out_17), .clk(in_8), .clr(in_9));  // open: en

  assign out_14 = out_10;

  // Notes on the sheet:
  //   PC
  //   LoadResult
  //   Alu Result
  //   INSTRUCTION
endmodule

module Control (
  input  in_1,
  input  isBgt,
  input  isUBranch,
  input  isLd,
  input  isSt,
  input  in_6,
  input  in_7,
  input  isRet,
  input  [12:0] in_9,
  input  Bubble,
  input  in_11,
  input  in_12,
  output [12:0] out_13,
  output out_14,
  output out_15,
  output out_16,
  output out_17,
  output out_18,
  output out_19,
  output out_20,
  output out_21
);

  wire [7:0] multiplexer_2_out;
  wire [12:0] multiplexer_1_out;

  Register #(.width(1)) register_1 (.D(multiplexer_2_out[7]), .Q(out_14), .clk(in_11), .clr(in_12));  // open: en
  Multiplexer #(.width(13)) multiplexer_1 (
    .in0(in_9), .in1({13{1'b0}}), .out(multiplexer_1_out), .sel(Bubble));  // open: en
  Register #(.width(13)) register_2 (.D(multiplexer_1_out), .Q(out_13), .clk(in_11), .clr(in_12));  // open: en
  Multiplexer #(.width(8), .enable("false")) multiplexer_2 (
    .in0({isRet, in_1, isBgt, isUBranch, isLd, isSt, in_6, in_7}), .in1({8{1'b0}}), .out(multiplexer_2_out),
    .sel(Bubble));
  Register #(.width(1)) register_3 (.D(multiplexer_2_out[6]), .Q(out_15), .clk(in_11), .clr(in_12));  // open: en
  Register #(.width(1)) register_4 (.D(multiplexer_2_out[5]), .Q(out_16), .clk(in_11), .clr(in_12));  // open: en
  Register #(.width(1)) register_5 (.D(multiplexer_2_out[4]), .Q(out_17), .clk(in_11), .clr(in_12));  // open: en
  Register #(.width(1)) register_6 (.D(multiplexer_2_out[3]), .Q(out_18), .clk(in_11), .clr(in_12));  // open: en
  Register #(.width(1)) register_7 (.D(multiplexer_2_out[2]), .Q(out_19), .clk(in_11), .clr(in_12));  // open: en
  Register #(.width(1)) register_8 (.D(multiplexer_2_out[1]), .Q(out_20), .clk(in_11), .clr(in_12));  // open: en
  Register #(.width(1)) register_9 (.D(multiplexer_2_out[0]), .Q(out_21), .clk(in_11), .clr(in_12));  // open: en

  // Notes on the sheet:
  //   ALU Signals
  //   isBeq
  //   isCall
  //   isWb
endmodule
